// Logisim project ALU.circ as structural Verilog: 13 circuits, main circuit CPU
module main (
  input  SUB,
  input  W_C,
  input  CAR_I,
  input  LOG_EN,
  input  LOG_SEL_1,
  input  LOG_SEL_0,
  input  RR_0,
  input  D_0,
  input  RR_1,
  input  D_1,
  input  RR_2,
  input  D_2,
  input  RR_3,
  input  D_3,
  output OUT_0,
  output OUT_1,
  output OUT_2,
  output OUT_3,
  output CAR_O
);

  wire and_1_out, and_2_out, and_3_out, and_4_out, and_5_out, and_6_out, and_7_out, and_8_out, and_9_out,
       and_10_out, and_11_out, and_12_out, and_13_out, and_14_out, and_15_out, and_16_out, and_17_out,
       and_18_out, and_20_out, and_21_out, and_22_out, and_23_out, and_24_out, and_25_out, and_26_out,
       and_27_out, and_28_out, and_29_out, and_30_out, and_31_out, and_32_out, and_33_out, and_34_out,
       and_35_out, and_36_out, and_37_out, and_38_out, not_1_out, not_2_out, not_3_out, not_4_out, or_1_out,
       or_2_out, or_3_out, or_4_out, or_5_out, or_6_out, or_7_out, or_8_out, or_9_out, or_10_out, or_11_out,
       or_12_out, or_13_out, or_14_out, or_15_out, or_16_out, or_17_out, xor_1_out, xor_2_out, xor_3_out,
       xor_4_out, xor_5_out, xor_6_out, xor_7_out, xor_8_out, xor_9_out, xor_10_out, xor_11_out, xor_12_out,
       xor_13_out, xor_14_out, xor_15_out, xor_16_out;

  xor xor_1 (xor_1_out, D_0, SUB);
  and and_1 (and_1_out, SUB, not_1_out);
  xor xor_2 (xor_2_out, D_1, SUB);
  xor xor_3 (xor_3_out, D_2, SUB);
  xor xor_4 (xor_4_out, D_3, SUB);
  not not_1 (not_1_out, W_C);
  or or_1 (or_1_out, and_1_out, and_2_out);
  and and_2 (and_2_out, W_C, CAR_I);
  xor xor_5 (xor_5_out, RR_0, xor_1_out);
  xor xor_6 (xor_6_out, RR_1, xor_2_out);
  xor xor_7 (xor_7_out, RR_2, xor_3_out);
  xor xor_8 (xor_8_out, RR_3, xor_4_out);
  xor xor_9 (xor_9_out, xor_5_out, or_1_out);
  and and_3 (and_3_out, xor_5_out, or_1_out);
  and and_4 (and_4_out, RR_0, xor_1_out);
  xor xor_10 (xor_10_out, xor_6_out, or_6_out);
  and and_5 (and_5_out, xor_6_out, or_6_out);
  and and_6 (and_6_out, RR_1, xor_2_out);
  xor xor_11 (xor_11_out, xor_7_out, or_7_out);
  and and_7 (and_7_out, xor_7_out, or_7_out);
  and and_8 (and_8_out, RR_2, xor_3_out);
  xor xor_12 (xor_12_out, xor_8_out, or_8_out);
  and and_9 (and_9_out, xor_8_out, or_8_out);
  and and_10 (and_10_out, RR_3, xor_4_out);
  and and_11 (and_11_out, RR_0, D_0);
  and and_12 (and_12_out, RR_1, D_1);
  and and_13 (and_13_out, RR_2, D_2);
  and and_14 (and_14_out, RR_3, D_3);
  or or_2 (or_2_out, RR_0, D_0);
  or or_3 (or_3_out, RR_1, D_1);
  or or_4 (or_4_out, RR_2, D_2);
  or or_5 (or_5_out, RR_3, D_3);
  xor xor_13 (xor_13_out, RR_0, D_0);
  xor xor_14 (xor_14_out, RR_1, D_1);
  xor xor_15 (xor_15_out, RR_2, D_2);
  xor xor_16 (xor_16_out, RR_3, D_3);
  or or_6 (or_6_out, and_3_out, and_4_out);
  or or_7 (or_7_out, and_5_out, and_6_out);
  or or_8 (or_8_out, and_7_out, and_8_out);
  or or_9 (or_9_out, and_9_out, and_10_out);
  not not_2 (not_2_out, LOG_EN);
  and and_15 (and_15_out, xor_9_out, not_2_out);
  and and_16 (and_16_out, xor_10_out, not_2_out);
  and and_17 (and_17_out, xor_11_out, not_2_out);
  and and_18 (and_18_out, xor_12_out, not_2_out);
  and and_19 (CAR_O, or_9_out, not_2_out);
  and and_20 (and_20_out, and_11_out, and_34_out);
  and and_21 (and_21_out, and_12_out, and_34_out);
  and and_22 (and_22_out, and_13_out, and_34_out);
  and and_23 (and_23_out, and_14_out, and_34_out);
  and and_24 (and_24_out, or_2_out, and_33_out);
  and and_25 (and_25_out, or_3_out, and_33_out);
  and and_26 (and_26_out, or_4_out, and_33_out);
  and and_27 (and_27_out, or_5_out, and_33_out);
  and and_28 (and_28_out, xor_13_out, and_32_out);
  and and_29 (and_29_out, xor_14_out, and_32_out);
  and and_30 (and_30_out, xor_15_out, and_32_out);
  and and_31 (and_31_out, xor_16_out, and_32_out);
  and and_32 (and_32_out, LOG_SEL_1, not_3_out);
  not not_3 (not_3_out, LOG_SEL_0);
  not not_4 (not_4_out, LOG_SEL_1);
  and and_33 (and_33_out, not_4_out, not_3_out);
  and and_34 (and_34_out, not_4_out, LOG_SEL_0);
  or or_10 (or_10_out, and_20_out, and_24_out);
  or or_11 (or_11_out, and_21_out, and_25_out);
  or or_12 (or_12_out, and_22_out, and_26_out);
  or or_13 (or_13_out, and_23_out, and_27_out);
  or or_14 (or_14_out, or_10_out, and_28_out);
  or or_15 (or_15_out, or_11_out, and_29_out);
  or or_16 (or_16_out, or_12_out, and_30_out);
  or or_17 (or_17_out, or_13_out, and_31_out);
  and and_35 (and_35_out, or_14_out, LOG_EN);
  and and_36 (and_36_out, or_15_out, LOG_EN);
  and and_37 (and_37_out, or_16_out, LOG_EN);
  and and_38 (and_38_out, or_17_out, LOG_EN);
  or or_18 (OUT_0, and_15_out, and_35_out);
  or or_19 (OUT_1, and_16_out, and_36_out);
  or or_20 (OUT_2, and_17_out, and_37_out);
  or or_21 (OUT_3, and_18_out, and_38_out);
endmodule

module CPU (
  input  EF0,
  input  EF1,
  input  D0,
  input  D1,
  input  D2,
  input  D3,
  input  RST,
  input  CLK,
  output O_D0_RR0,
  output O_D1_RR1,
  output O_D2_RR2,
  output O_D3_RR3,
  output O_4_MAR,
  output O_5_WRITE,
  output O_6_JMP,
  output O_7_I
);

  wire and_1_out, and_2_out, and_3_out, and_4_out, and_5_out, and_6_out, and_7_out, and_8_out, and_9_out,
       and_10_out, and_11_out, and_12_out, and_13_out, and_14_out, and_15_out, and_16_out, and_17_out,
       and_18_out, and_19_out, and_20_out, and_21_out, and_22_out, and_23_out, and_24_out, and_25_out,
       and_26_out, and_27_out, and_28_out, and_29_out, and_30_out, and_31_out, and_32_out, and_33_out,
       and_34_out, and_35_out, and_36_out, and_37_out, and_38_out, and_39_out, and_40_out, and_41_out,
       and_42_out, and_43_out, and_44_out, and_45_out, and_46_out, and_47_out, and_48_out, and_49_out,
       and_50_out, and_51_out, and_52_out, and_53_out, and_54_out, d_ff_1_q, d_ff_2_q, d_ff_2_qn, d_ff_3_q,
       d_ff_4_q, d_ff_5_q, d_ff_6_q, d_ff_7_q, d_ff_8_q, d_ff_9_q, d_ff_10_q, d_ff_11_q, d_ff_12_q,
       d_ff_13_q, d_ff_14_q, d_ff_15_q, d_ff_16_q, d_ff_17_q, d_ff_18_q, d_ff_19_q, d_ff_20_q, d_ff_21_q,
       d_ff_22_q, d_ff_23_q, d_ff_24_q, d_ff_25_q, d_ff_26_q, d_ff_27_q, dest_reg_sel_1_s0,
       dest_reg_sel_1_s1, dest_reg_sel_1_s2, eq_0_1_is_zero, inst_dec_1_ari, inst_dec_1_i0, inst_dec_1_i1,
       inst_dec_1_i2, inst_dec_1_i3, inst_dec_1_jmp, inst_dec_1_ld, inst_dec_1_ldd, inst_dec_1_log,
       inst_dec_1_sei, inst_dec_1_smh, inst_dec_1_sml, inst_dec_1_str, inst_dec_1_w_car, main_1_car_o,
       main_1_out_0, main_1_out_1, main_1_out_2, main_1_out_3, multiply_1_r0, multiply_1_r1, multiply_1_r2,
       multiply_1_r3, nand_1_out, nor_1_out, nor_2_out, not_1_out, not_2_out, not_3_out, not_4_out,
       not_5_out, not_6_out, or_1_out, or_2_out, or_3_out, or_4_out, or_5_out, or_6_out, or_7_out, or_8_out,
       or_9_out, or_10_out, or_11_out, or_12_out, or_13_out, or_14_out, or_15_out, or_16_out, toggle_1_clk1,
       toggle_1_clk2, toggle_1_o_s;

  and and_1 (and_1_out, toggle_1_clk2, not_1_out);
  D_Flip_Flop d_ff_1 (.D(and_1_out), .clk(CLK), .Q(d_ff_1_q));  // open: Qn, preset, reset
  and and_2 (and_2_out, and_44_out, EF0);
  and and_3 (and_3_out, and_44_out, EF1);
  and and_4 (and_4_out, nand_1_out, D0);
  and and_5 (and_5_out, nand_1_out, D1);
  and and_6 (and_6_out, nand_1_out, D2);
  and and_7 (and_7_out, nand_1_out, D3);
  not not_1 (not_1_out, inst_dec_1_ldd);
  not not_2 (not_2_out, and_1_out);
  or or_1 (or_1_out, and_52_out, and_3_out);
  D_Flip_Flop d_ff_2 (
    .D(inst_dec_1_sei), .clk(and_8_out), .Q(d_ff_2_q), .Qn(d_ff_2_qn), .reset(and_9_out));  // open: preset
  and and_8 (and_8_out, d_ff_1_q, not_2_out);
  and and_9 (and_9_out, RST, CLK);
  or or_2 (or_2_out, and_51_out, and_2_out);
  inst_dec inst_dec_1 (
    .D0(D0), .D1(D1), .D2(D2), .D3(D3), .CLK1(toggle_1_clk1), .RST(RST), .CLK(CLK), .SMH(inst_dec_1_smh),
    .LOG(inst_dec_1_log), .LD(inst_dec_1_ld), .STR(inst_dec_1_str), .SEI(inst_dec_1_sei),
    .SML(inst_dec_1_sml), .ARI(inst_dec_1_ari), .W_CAR(inst_dec_1_w_car), .I0(inst_dec_1_i0),
    .I1(inst_dec_1_i1), .I2(inst_dec_1_i2), .I3(inst_dec_1_i3), .JMP(inst_dec_1_jmp), .LDD(inst_dec_1_ldd));
  // NoConnect on inst_dec_1_i2
  // NoConnect on inst_dec_1_i3
  toggle toggle_1 (.RST(RST), .CLK(CLK), .O_S(toggle_1_o_s), .CLK1(toggle_1_clk1), .CLK2(toggle_1_clk2));
  or or_3 (or_3_out, or_2_out, and_4_out);
  or or_4 (or_4_out, or_1_out, and_5_out);
  or or_5 (or_5_out, and_53_out, and_6_out);
  or or_6 (or_6_out, and_54_out, and_7_out);
  or or_7 (or_7_out, inst_dec_1_sml, inst_dec_1_smh);
  or or_8 (or_8_out, inst_dec_1_str, inst_dec_1_ld);
  or or_9 (or_9_out, inst_dec_1_log, inst_dec_1_ari);
  main main_1 (
    .SUB(inst_dec_1_i0), .W_C(inst_dec_1_w_car), .CAR_I(d_ff_7_q), .LOG_EN(inst_dec_1_log),
    .LOG_SEL_1(inst_dec_1_i1), .LOG_SEL_0(inst_dec_1_i0), .RR_0(and_12_out), .D_0(or_3_out),
    .RR_1(and_13_out), .D_1(or_4_out), .RR_2(and_14_out), .D_2(or_5_out), .RR_3(and_15_out), .D_3(or_6_out),
    .OUT_0(main_1_out_0), .OUT_1(main_1_out_1), .OUT_2(main_1_out_2), .OUT_3(main_1_out_3),
    .CAR_O(main_1_car_o));
  and and_10 (and_10_out, toggle_1_clk2, or_9_out);
  and and_11 (and_11_out, toggle_1_clk2, inst_dec_1_ari);
  and and_12 (and_12_out, d_ff_3_q, not_3_out);
  and and_13 (and_13_out, d_ff_4_q, not_3_out);
  and and_14 (and_14_out, d_ff_5_q, not_3_out);
  and and_15 (and_15_out, d_ff_6_q, not_3_out);
  not not_3 (not_3_out, inst_dec_1_ld);
  D_Flip_Flop d_ff_3 (.D(main_1_out_0), .clk(and_10_out), .Q(d_ff_3_q));  // open: Qn, preset, reset
  D_Flip_Flop d_ff_4 (.D(main_1_out_1), .clk(and_10_out), .Q(d_ff_4_q));  // open: Qn, preset, reset
  D_Flip_Flop d_ff_5 (.D(main_1_out_2), .clk(and_10_out), .Q(d_ff_5_q));  // open: Qn, preset, reset
  D_Flip_Flop d_ff_6 (.D(main_1_out_3), .clk(and_10_out), .Q(d_ff_6_q));  // open: Qn, preset, reset
  D_Flip_Flop d_ff_7 (.D(main_1_car_o), .clk(and_11_out), .Q(d_ff_7_q));  // open: Qn, preset, reset
  nor nor_1 (nor_1_out, inst_dec_1_i0, inst_dec_1_i1);
  and and_16 (and_16_out, inst_dec_1_i0, d_ff_7_q);
  and and_17 (and_17_out, inst_dec_1_i1, eq_0_1_is_zero);
  and and_18 (and_18_out, nor_1_out, inst_dec_1_jmp);
  and and_19 (and_19_out, inst_dec_1_jmp, and_16_out);
  and and_20 (and_20_out, inst_dec_1_jmp, and_17_out);
  or or_10 (or_10_out, and_18_out, and_19_out);
  and and_21 (and_21_out, d_ff_3_q, d_ff_2_qn);
  and and_22 (and_22_out, d_ff_4_q, d_ff_2_qn);
  and and_23 (and_23_out, d_ff_5_q, d_ff_2_qn);
  and and_24 (and_24_out, d_ff_6_q, d_ff_2_qn);
  or or_11 (or_11_out, or_10_out, and_20_out);
  eq_0 eq_0_1 (.D0(d_ff_3_q), .D1(d_ff_4_q), .D2(d_ff_5_q), .D3(d_ff_6_q), .is_zero(eq_0_1_is_zero));
  dest_reg_sel dest_reg_sel_1 (
    .CLK1(toggle_1_clk1), .LDD(inst_dec_1_ldd), .CLK(CLK), .RST(RST), .S0(dest_reg_sel_1_s0),
    .S1(dest_reg_sel_1_s1), .S2(dest_reg_sel_1_s2));
  or or_12 (or_12_out, and_21_out, and_25_out);
  and and_25 (and_25_out, d_ff_2_q, or_3_out);
  or or_13 (or_13_out, and_22_out, and_26_out);
  or or_14 (or_14_out, and_23_out, and_27_out);
  and and_26 (and_26_out, d_ff_2_q, or_4_out);
  and and_27 (and_27_out, d_ff_2_q, or_5_out);
  or or_15 (or_15_out, and_24_out, and_31_out);
  not not_4 (not_4_out, toggle_1_clk1);
  and and_28 (and_28_out, inst_dec_1_ldd, dest_reg_sel_1_s0);
  and and_29 (and_29_out, inst_dec_1_ldd, dest_reg_sel_1_s1);
  and and_30 (and_30_out, inst_dec_1_ldd, dest_reg_sel_1_s2);
  and and_31 (and_31_out, d_ff_2_q, or_6_out);
  and and_32 (and_32_out, inst_dec_1_sml, not_4_out);
  and and_33 (and_33_out, inst_dec_1_smh, not_4_out);
  and and_34 (and_34_out, toggle_1_clk2, and_28_out);
  and and_35 (and_35_out, toggle_1_clk2, and_29_out);
  and and_36 (and_36_out, toggle_1_clk2, and_30_out);
  D_Flip_Flop d_ff_8 (.D(or_12_out), .clk(and_32_out), .Q(d_ff_8_q));  // open: Qn, preset, reset
  D_Flip_Flop d_ff_9 (.D(or_13_out), .clk(and_32_out), .Q(d_ff_9_q));  // open: Qn, preset, reset
  D_Flip_Flop d_ff_10 (.D(or_14_out), .clk(and_32_out), .Q(d_ff_10_q));  // open: Qn, preset, reset
  D_Flip_Flop d_ff_11 (.D(or_15_out), .clk(and_32_out), .Q(d_ff_11_q));  // open: Qn, preset, reset
  D_Flip_Flop d_ff_12 (.D(or_12_out), .clk(and_33_out), .Q(d_ff_12_q));  // open: Qn, preset, reset
  D_Flip_Flop d_ff_13 (.D(or_13_out), .clk(and_33_out), .Q(d_ff_13_q));  // open: Qn, preset, reset
  D_Flip_Flop d_ff_14 (.D(or_14_out), .clk(and_33_out), .Q(d_ff_14_q));  // open: Qn, preset, reset
  D_Flip_Flop d_ff_15 (.D(or_15_out), .clk(and_33_out), .Q(d_ff_15_q));  // open: Qn, preset, reset
  D_Flip_Flop d_ff_16 (.D(or_12_out), .clk(and_34_out), .Q(d_ff_16_q));  // open: Qn, preset, reset
  D_Flip_Flop d_ff_17 (.D(or_13_out), .clk(and_34_out), .Q(d_ff_17_q));  // open: Qn, preset, reset
  D_Flip_Flop d_ff_18 (.D(or_14_out), .clk(and_34_out), .Q(d_ff_18_q));  // open: Qn, preset, reset
  D_Flip_Flop d_ff_19 (.D(or_15_out), .clk(and_34_out), .Q(d_ff_19_q));  // open: Qn, preset, reset
  D_Flip_Flop d_ff_20 (.D(or_12_out), .clk(and_35_out), .Q(d_ff_20_q));  // open: Qn, preset, reset
  D_Flip_Flop d_ff_21 (.D(or_13_out), .clk(and_35_out), .Q(d_ff_21_q));  // open: Qn, preset, reset
  D_Flip_Flop d_ff_22 (.D(or_14_out), .clk(and_35_out), .Q(d_ff_22_q));  // open: Qn, preset, reset
  D_Flip_Flop d_ff_23 (.D(or_15_out), .clk(and_35_out), .Q(d_ff_23_q));  // open: Qn, preset, reset
  D_Flip_Flop d_ff_24 (.D(or_12_out), .clk(and_36_out), .Q(d_ff_24_q));  // open: Qn, preset, reset
  D_Flip_Flop d_ff_25 (.D(or_13_out), .clk(and_36_out), .Q(d_ff_25_q));  // open: Qn, preset, reset
  D_Flip_Flop d_ff_26 (.D(or_14_out), .clk(and_36_out), .Q(d_ff_26_q));  // open: Qn, preset, reset
  D_Flip_Flop d_ff_27 (.D(or_15_out), .clk(and_36_out), .Q(d_ff_27_q));  // open: Qn, preset, reset
  and and_37 (and_37_out, inst_dec_1_str, not_5_out);
  not not_5 (not_5_out, and_48_out);
  output_logic output_logic_1 (
    .O_S(toggle_1_o_s), .DO_JMP(or_11_out), .DEST_0(d_ff_16_q), .DEST_1(d_ff_17_q), .DEST_2(d_ff_18_q),
    .DEST_3(d_ff_19_q), .DEST_4(d_ff_20_q), .DEST_5(d_ff_21_q), .DEST_6(d_ff_22_q), .DEST_7(d_ff_23_q),
    .MAR_0(d_ff_8_q), .MAR_1(d_ff_9_q), .MAR_2(d_ff_10_q), .MAR_3(d_ff_11_q), .MAR_4(d_ff_12_q),
    .MAR_5(d_ff_13_q), .MAR_6(d_ff_14_q), .MAR_7(d_ff_15_q), .DEST_8(d_ff_24_q), .DEST_9(d_ff_25_q),
    .DEST_10(d_ff_26_q), .DEST_11(d_ff_27_q), .RR_0(d_ff_3_q), .RR_1(d_ff_4_q), .RR_2(d_ff_5_q),
    .RR_3(d_ff_6_q), .MAR(or_7_out), .WRITE(and_37_out), .JMP(or_11_out), .F_I(d_ff_2_q), .OUT_0(O_D0_RR0),
    .OUT_1(O_D1_RR1), .OUT_2(O_D2_RR2), .OUT_3(O_D3_RR3), .OUT_4(O_4_MAR), .OUT_5(O_5_WRITE),
    .OUT_6(O_6_JMP), .OUT_7(O_7_I));
  and and_38 (and_38_out, d_ff_8_q, d_ff_9_q);
  and and_39 (and_39_out, d_ff_10_q, d_ff_11_q);
  nor nor_2 (nor_2_out, d_ff_10_q, d_ff_11_q);
  and and_40 (and_40_out, d_ff_12_q, d_ff_13_q);
  and and_41 (and_41_out, d_ff_14_q, d_ff_15_q);
  and and_42 (and_42_out, and_38_out, and_39_out);
  and and_43 (and_43_out, and_40_out, and_41_out);
  and and_44 (and_44_out, and_42_out, and_45_out);
  and and_45 (and_45_out, and_43_out, or_8_out);
  nand nand_1 (nand_1_out, or_16_out, and_45_out);
  or or_16 (or_16_out, and_42_out, d_ff_9_q);
  not not_6 (not_6_out, d_ff_9_q);
  and and_46 (and_46_out, not_6_out, and_45_out);
  and and_47 (and_47_out, d_ff_9_q, and_45_out);
  and and_48 (and_48_out, nor_2_out, and_46_out);
  and and_49 (and_49_out, toggle_1_clk2, and_48_out);
  and and_50 (and_50_out, and_47_out, nor_2_out);
  multiply multiply_1 (
    .DIN0(or_12_out), .DIN1(or_13_out), .DIN2(or_14_out), .DIN3(or_15_out), .RSEL(d_ff_8_q),
    .LOAD(and_49_out), .MUL_CLK(CLK), .R0(multiply_1_r0), .R1(multiply_1_r1), .R2(multiply_1_r2),
    .R3(multiply_1_r3));
  and and_51 (and_51_out, multiply_1_r0, and_50_out);
  and and_52 (and_52_out, multiply_1_r1, and_50_out);
  and and_53 (and_53_out, multiply_1_r2, and_50_out);
  and and_54 (and_54_out, multiply_1_r3, and_50_out);

  // Notes on the sheet:
  //   ~F_I
  //   F_I
  //   MAR LOW
  //   MAR HIGH
  //   DEST 0
  //   DEST 4
  //   DEST 8
endmodule

module clock_gen (
  input  RST,
  input  CLK,
  output O_S,
  output CLK1,
  output CLK2
);

  wire and_1_out, d_ff_2_q, d_ff_4_q, or_1_out;

  D_Flip_Flop d_ff_1 (.D(d_ff_4_q), .clk(CLK), .Q(CLK1), .reset(and_1_out));  // open: Qn, preset
  and and_1 (and_1_out, RST, CLK);
  or or_1 (or_1_out, CLK1, CLK2);
  D_Flip_Flop d_ff_2 (.D(CLK1), .clk(CLK), .Q(d_ff_2_q), .reset(and_1_out));  // open: Qn, preset
  T_Flip_Flop t_ff_1 (.T(1'b1), .clk(or_1_out), .Q(O_S), .preset(and_1_out));  // open: Qn, reset
  D_Flip_Flop d_ff_3 (.D(d_ff_2_q), .clk(CLK), .Q(CLK2), .reset(and_1_out));  // open: Qn, preset
  D_Flip_Flop d_ff_4 (.D(CLK2), .clk(CLK), .Q(d_ff_4_q), .preset(and_1_out));  // open: Qn, reset
endmodule

module eq_0 (
  input  D0,
  input  D1,
  input  D2,
  input  D3,
  output is_zero
);

  wire or_1_out, or_2_out;

  or or_1 (or_1_out, D0, D1);
  or or_2 (or_2_out, D2, D3);
  nor nor_1 (is_zero, or_1_out, or_2_out);
endmodule

module output_logic (
  input  O_S,
  input  DO_JMP,
  input  DEST_0,
  input  DEST_1,
  input  DEST_2,
  input  DEST_3,
  input  DEST_4,
  input  DEST_5,
  input  DEST_6,
  input  DEST_7,
  input  MAR_0,
  input  MAR_1,
  input  MAR_2,
  input  MAR_3,
  input  MAR_4,
  input  MAR_5,
  input  MAR_6,
  input  MAR_7,
  input  DEST_8,
  input  DEST_9,
  input  DEST_10,
  input  DEST_11,
  input  RR_0,
  input  RR_1,
  input  RR_2,
  input  RR_3,
  input  MAR,
  input  WRITE,
  input  JMP,
  input  F_I,
  output OUT_0,
  output OUT_1,
  output OUT_2,
  output OUT_3,
  output OUT_4,
  output OUT_5,
  output OUT_6,
  output OUT_7
);

  wire and_1_out, and_2_out, and_3_out, and_4_out, and_5_out, and_6_out, and_7_out, and_8_out, and_9_out,
       and_10_out, and_11_out, and_12_out, and_13_out, and_14_out, and_15_out, and_16_out, and_17_out,
       and_18_out, and_19_out, and_20_out, and_21_out, and_22_out, and_23_out, and_24_out, and_25_out,
       and_26_out, and_27_out, and_28_out, and_29_out, and_30_out, and_31_out, and_32_out, and_33_out,
       and_34_out, and_35_out, and_36_out, and_37_out, and_38_out, and_39_out, and_40_out, not_1_out,
       not_2_out, or_1_out, or_2_out, or_3_out, or_4_out, or_5_out, or_6_out, or_7_out, or_8_out, or_9_out,
       or_10_out, or_11_out, or_12_out;

  not not_1 (not_1_out, DO_JMP);
  and and_1 (and_1_out, DEST_0, DO_JMP);
  and and_2 (and_2_out, DEST_1, DO_JMP);
  and and_3 (and_3_out, DEST_2, DO_JMP);
  and and_4 (and_4_out, DEST_3, DO_JMP);
  and and_5 (and_5_out, DEST_4, DO_JMP);
  and and_6 (and_6_out, DEST_5, DO_JMP);
  and and_7 (and_7_out, DEST_6, DO_JMP);
  and and_8 (and_8_out, DEST_7, DO_JMP);
  and and_9 (and_9_out, MAR_0, not_1_out);
  and and_10 (and_10_out, MAR_1, not_1_out);
  and and_11 (and_11_out, MAR_2, not_1_out);
  and and_12 (and_12_out, MAR_3, not_1_out);
  and and_13 (and_13_out, MAR_4, not_1_out);
  and and_14 (and_14_out, MAR_5, not_1_out);
  and and_15 (and_15_out, MAR_6, not_1_out);
  and and_16 (and_16_out, MAR_7, not_1_out);
  and and_17 (and_17_out, DEST_8, DO_JMP);
  and and_18 (and_18_out, DEST_9, DO_JMP);
  and and_19 (and_19_out, DEST_10, DO_JMP);
  and and_20 (and_20_out, DEST_11, DO_JMP);
  and and_21 (and_21_out, RR_0, not_1_out);
  and and_22 (and_22_out, RR_1, not_1_out);
  and and_23 (and_23_out, RR_2, not_1_out);
  and and_24 (and_24_out, RR_3, not_1_out);
  or or_1 (or_1_out, and_17_out, and_21_out);
  or or_2 (or_2_out, and_18_out, and_22_out);
  or or_3 (or_3_out, and_19_out, and_23_out);
  or or_4 (or_4_out, and_20_out, and_24_out);
  or or_5 (or_5_out, and_1_out, and_9_out);
  or or_6 (or_6_out, and_2_out, and_10_out);
  or or_7 (or_7_out, and_3_out, and_11_out);
  or or_8 (or_8_out, and_4_out, and_12_out);
  or or_9 (or_9_out, and_5_out, and_13_out);
  or or_10 (or_10_out, and_6_out, and_14_out);
  or or_11 (or_11_out, and_7_out, and_15_out);
  or or_12 (or_12_out, and_8_out, and_16_out);
  not not_2 (not_2_out, O_S);
  and and_25 (and_25_out, or_5_out, not_2_out);
  and and_26 (and_26_out, or_6_out, not_2_out);
  and and_27 (and_27_out, or_7_out, not_2_out);
  and and_28 (and_28_out, or_8_out, not_2_out);
  and and_29 (and_29_out, or_9_out, not_2_out);
  and and_30 (and_30_out, or_10_out, not_2_out);
  and and_31 (and_31_out, or_11_out, not_2_out);
  and and_32 (and_32_out, or_12_out, not_2_out);
  and and_33 (and_33_out, or_1_out, O_S);
  and and_34 (and_34_out, or_2_out, O_S);
  and and_35 (and_35_out, or_3_out, O_S);
  and and_36 (and_36_out, or_4_out, O_S);
  and and_37 (and_37_out, MAR, O_S);
  and and_38 (and_38_out, WRITE, O_S);
  and and_39 (and_39_out, JMP, O_S);
  and and_40 (and_40_out, F_I, O_S);
  or or_13 (OUT_0, and_25_out, and_33_out);
  or or_14 (OUT_1, and_26_out, and_34_out);
  or or_15 (OUT_2, and_27_out, and_35_out);
  or or_16 (OUT_3, and_28_out, and_36_out);
  or or_17 (OUT_4, and_29_out, and_37_out);
  or or_18 (OUT_5, and_30_out, and_38_out);
  or or_19 (OUT_6, and_31_out, and_39_out);
  or or_20 (OUT_7, and_32_out, and_40_out);
endmodule

module dest_reg_sel (
  input  CLK1,
  input  LDD,
  input  CLK,
  input  RST,
  output S0,
  output S1,
  output S2
);

  wire and_1_out, and_2_out, d_ff_1_qn, d_ff_2_qn, d_ff_3_qn, not_1_out, not_2_out, not_3_out, not_4_out;

  D_Flip_Flop d_ff_1 (.D(not_4_out), .clk(and_2_out), .Q(S0), .Qn(d_ff_1_qn), .reset(and_1_out));  // open: preset
  and and_1 (and_1_out, CLK, RST);
  not not_1 (not_1_out, d_ff_1_qn);
  not not_2 (not_2_out, CLK1);
  D_Flip_Flop d_ff_2 (.D(not_1_out), .clk(and_2_out), .Q(S1), .Qn(d_ff_2_qn), .reset(and_1_out));  // open: preset
  and and_2 (and_2_out, not_2_out, LDD);
  not not_3 (not_3_out, d_ff_2_qn);
  not not_4 (not_4_out, d_ff_3_qn);
  D_Flip_Flop d_ff_3 (.D(not_3_out), .clk(and_2_out), .Q(S2), .Qn(d_ff_3_qn), .preset(and_1_out));  // open: reset
endmodule

module inst_dec (
  input  D0,
  input  D1,
  input  D2,
  input  D3,
  input  CLK1,
  input  RST,
  input  CLK,
  output SMH,
  output LOG,
  output LD,
  output STR,
  output SEI,
  output SML,
  output ARI,
  output W_CAR,
  output I0,
  output I1,
  output I2,
  output I3,
  output JMP,
  output LDD
);

  wire and_1_out, and_2_out, and_3_out, and_9_out, and_11_out, and_14_out, and_16_out, and_18_out, d_ff_1_qn,
       d_ff_2_qn, d_ff_3_qn, d_ff_4_qn, nand_1_out, nor_1_out, not_1_out, not_2_out, or_1_out;

  D_Flip_Flop d_ff_1 (.D(D0), .clk(CLK1), .Q(I0), .Qn(d_ff_1_qn), .reset(and_1_out));  // open: preset
  D_Flip_Flop d_ff_2 (.D(D1), .clk(CLK1), .Q(I1), .Qn(d_ff_2_qn), .reset(and_1_out));  // open: preset
  D_Flip_Flop d_ff_3 (.D(D2), .clk(CLK1), .Q(I2), .Qn(d_ff_3_qn), .reset(and_1_out));  // open: preset
  D_Flip_Flop d_ff_4 (.D(D3), .clk(CLK1), .Q(I3), .Qn(d_ff_4_qn), .reset(and_1_out));  // open: preset
  and and_1 (and_1_out, RST, CLK);
  and and_2 (and_2_out, d_ff_4_qn, I2);
  and and_3 (and_3_out, I0, I1);
  and and_4 (ARI, d_ff_3_qn, I3);
  nand nand_1 (nand_1_out, I0, I1);
  and and_5 (W_CAR, ARI, I1);
  not not_1 (not_1_out, and_3_out);
  and and_6 (JMP, and_2_out, not_1_out);
  and and_7 (LDD, and_3_out, and_2_out);
  and and_8 (LOG, nand_1_out, or_1_out);
  or or_1 (or_1_out, and_9_out, LD);
  and and_9 (and_9_out, I2, I3);
  and and_10 (SMH, not_2_out, or_1_out);
  not not_2 (not_2_out, nand_1_out);
  nor nor_1 (nor_1_out, I2, I3);
  and and_11 (and_11_out, d_ff_1_qn, d_ff_2_qn);
  and and_12 (LD, and_11_out, nor_1_out);
  and and_13 (STR, and_14_out, nor_1_out);
  and and_14 (and_14_out, I0, d_ff_2_qn);
  and and_15 (SEI, and_16_out, nor_1_out);
  and and_16 (and_16_out, d_ff_1_qn, I1);
  and and_17 (SML, and_18_out, nor_1_out);
  and and_18 (and_18_out, I0, I1);
endmodule

module test_board (
);

  wire CPU_1_o_4_mar, CPU_1_o_5_write, CPU_1_o_6_jmp, CPU_1_o_7_i, DipSwitch_1_sw7, n7400_1_pin4,
       n7400_1_pin6, n7400_1_pin8, n7400_1_pin10, n7400_1_pin11, n7400_1_pin13, n7408_1_pin3, n7408_1_pin8,
       n7408_2_pin11, n7432_1_pin11, n7432_1_pin12, n7432_1_pin13, n7474_1_pin2, n7474_1_pin4, n7474_1_pin5,
       n7474_1_pin9, n7474_1_pin10, n7474_1_pin12, n7474_2_pin4, n7474_2_pin10, n74163_1_pin1, n74163_1_pin2,
       n74163_1_pin3, n74163_1_pin4, n74163_1_pin5, n74163_1_pin6, n74163_1_pin7, n74163_1_pin9,
       n74163_1_pin10, n74163_1_pin15, n74163_2_pin3, n74163_2_pin4, n74163_2_pin5, n74163_2_pin6,
       n74163_2_pin15, n74163_3_pin3, n74163_3_pin4, n74163_3_pin5, n74163_3_pin6, n74244_1_pin1,
       n74244_1_pin3, n74244_1_pin5, n74244_1_pin7, n74244_1_pin9, n74244_1_pin19;
  wire [3:0] n74244_2_pin18;
  wire [7:0] n74273_2_pin2, ROM_1_data;
  wire [11:0] n74163_1_pin14;

  _74163 u_74163_1 (
    .pin1(n74163_1_pin1), .pin2(n74163_1_pin2), .pin3(n74163_1_pin3), .pin4(n74163_1_pin4),
    .pin5(n74163_1_pin5), .pin6(n74163_1_pin6), .pin7(n74163_1_pin7), .pin15(n74163_1_pin15),
    .pin14(n74163_1_pin14[0]), .pin13(n74163_1_pin14[1]), .pin12(n74163_1_pin14[2]),
    .pin11(n74163_1_pin14[3]), .pin10(n74163_1_pin10), .pin9(n74163_1_pin9));
  _74163 u_74163_2 (
    .pin1(n74163_1_pin1), .pin2(n74163_1_pin2), .pin3(n74163_2_pin3), .pin4(n74163_2_pin4),
    .pin5(n74163_2_pin5), .pin6(n74163_2_pin6), .pin7(n74163_1_pin7), .pin15(n74163_2_pin15),
    .pin14(n74163_1_pin14[4]), .pin13(n74163_1_pin14[5]), .pin12(n74163_1_pin14[6]),
    .pin11(n74163_1_pin14[7]), .pin10(n74163_1_pin15), .pin9(n74163_1_pin9));
  _74163 u_74163_3 (
    .pin1(n74163_1_pin1), .pin2(n74163_1_pin2), .pin3(n74163_3_pin3), .pin4(n74163_3_pin4),
    .pin5(n74163_3_pin5), .pin6(n74163_3_pin6), .pin7(n74163_1_pin7), .pin14(n74163_1_pin14[8]),
    .pin13(n74163_1_pin14[9]), .pin12(n74163_1_pin14[10]), .pin11(n74163_1_pin14[11]),
    .pin10(n74163_2_pin15), .pin9(n74163_1_pin9));  // open: pin15
  DipSwitch DipSwitch_1 (.sw7(DipSwitch_1_sw7));  // open: sw1, sw2, sw3, sw4, sw5, sw6, sw8
  _7400 u_7400_1 (
    .pin1(DipSwitch_1_sw7), .pin2(DipSwitch_1_sw7), .pin3(n74163_1_pin1), .pin4(n7400_1_pin4),
    .pin5(n7400_1_pin4), .pin6(n7400_1_pin6), .pin13(n7400_1_pin13), .pin12(n7400_1_pin13),
    .pin11(n7400_1_pin11), .pin10(n7400_1_pin10), .pin9(n7400_1_pin10), .pin8(n7400_1_pin8));
  Clock clock_1 (.out(n7400_1_pin4));
  ROM #(.addrWidth(12)) ROM_1 (.addr(n74163_1_pin14), .data(ROM_1_data));
  _7474 u_7474_1 (
    .pin1(n74163_1_pin1), .pin2(n7474_1_pin2), .pin3(n7400_1_pin4), .pin4(n7474_1_pin4), .pin5(n7474_1_pin5),
    .pin6(n7474_1_pin2), .pin13(n74163_1_pin1), .pin12(n7474_1_pin12), .pin11(n7400_1_pin8),
    .pin10(n7474_1_pin10), .pin9(n7474_1_pin9), .pin8(n7474_1_pin12));
  _74244 u_74244_1 (
    .pin1(n74244_1_pin1), .pin2(ROM_1_data[7]), .pin3(n74244_1_pin3), .pin4(ROM_1_data[6]),
    .pin5(n74244_1_pin5), .pin6(ROM_1_data[5]), .pin7(n74244_1_pin7), .pin8(ROM_1_data[4]),
    .pin9(n74244_1_pin9), .pin19(n74244_1_pin19), .pin18(n74244_1_pin3), .pin17(ROM_1_data[3]),
    .pin16(n74244_1_pin5), .pin15(ROM_1_data[2]), .pin14(n74244_1_pin7), .pin13(ROM_1_data[1]),
    .pin12(n74244_1_pin9), .pin11(ROM_1_data[0]));
  _7408 u_7408_1 (
    .pin1(n7474_1_pin5), .pin2(n7400_1_pin6), .pin3(n7408_1_pin3), .pin4(n7400_1_pin10),
    .pin5(n7474_1_pin12), .pin6(n74163_1_pin2), .pin13(n7400_1_pin6), .pin12(n7474_1_pin2),
    .pin11(n7400_1_pin10), .pin10(n7400_1_pin10), .pin9(n7474_1_pin9), .pin8(n7408_1_pin8));
  _7432 u_7432_1 (
    .pin13(n7432_1_pin13), .pin12(n7432_1_pin12), .pin11(n7432_1_pin11));  // open: pin1, pin2, pin3, pin4, pin5, pin6, pin10, pin9, pin8
  CPU CPU_1 (
    .EF0(1'b1), .EF1(1'b1), .D0(n74244_1_pin9), .D1(n74244_1_pin7), .D2(n74244_1_pin5), .D3(n74244_1_pin3),
    .RST(DipSwitch_1_sw7), .CLK(n7400_1_pin4), .O_D0_RR0(n74163_3_pin3), .O_D1_RR1(n74163_3_pin4),
    .O_D2_RR2(n74163_3_pin5), .O_D3_RR3(n74163_3_pin6), .O_4_MAR(CPU_1_o_4_mar), .O_5_WRITE(CPU_1_o_5_write),
    .O_6_JMP(CPU_1_o_6_jmp), .O_7_I(CPU_1_o_7_i));
  _7408 u_7408_2 (
    .pin13(n74163_1_pin2), .pin12(CPU_1_o_4_mar), .pin11(n7408_2_pin11), .pin10(CPU_1_o_5_write),
    .pin9(n74163_1_pin2), .pin8(n7400_1_pin13));  // open: pin1, pin2, pin3, pin4, pin5, pin6
  _7400 u_7400_2 (
    .pin1(CPU_1_o_6_jmp), .pin2(CPU_1_o_6_jmp), .pin3(n74163_1_pin9), .pin10(n7432_1_pin13),
    .pin9(n74244_1_pin19), .pin8(n74244_1_pin1));  // open: pin4, pin5, pin6, pin13, pin12, pin11
  _74244 u_74244_2 (
    .pin1(n7400_1_pin11), .pin2(n74163_3_pin3), .pin3(n74244_1_pin9), .pin4(n74163_3_pin4),
    .pin5(n74244_1_pin7), .pin6(n74163_3_pin5), .pin7(n74244_1_pin5), .pin8(n74163_3_pin6),
    .pin9(n74244_1_pin3), .pin19(n7432_1_pin11), .pin18(n74244_2_pin18[0]), .pin17(n74244_2_pin18[0]),
    .pin16(n74244_2_pin18[1]), .pin15(n74244_2_pin18[1]), .pin14(n74244_2_pin18[2]),
    .pin13(n74244_2_pin18[2]), .pin12(n74244_2_pin18[3]), .pin11(n74244_2_pin18[3]));
  _7474 u_7474_2 (
    .pin1(n74163_1_pin1), .pin2(CPU_1_o_7_i), .pin3(n74163_1_pin2), .pin4(n7474_2_pin4),
    .pin5(n7432_1_pin13), .pin13(n74163_1_pin1), .pin12(n7432_1_pin12), .pin11(n7408_1_pin3),
    .pin10(n7474_2_pin10), .pin9(n74244_1_pin19), .pin8(n7432_1_pin12));  // open: pin6
  _74273 u_74273_1 (
    .pin1(n74163_1_pin1), .pin2(n74163_1_pin3), .pin3(n74163_3_pin3), .pin4(n74163_3_pin4),
    .pin5(n74163_1_pin4), .pin6(n74163_1_pin5), .pin7(n74163_3_pin5), .pin8(n74163_3_pin6),
    .pin9(n74163_1_pin6), .pin19(n74163_2_pin6), .pin18(CPU_1_o_7_i), .pin17(CPU_1_o_6_jmp),
    .pin16(n74163_2_pin5), .pin15(n74163_2_pin4), .pin14(CPU_1_o_5_write), .pin13(CPU_1_o_4_mar),
    .pin12(n74163_2_pin3), .pin11(n7408_1_pin8));
  Pull_Resistor pull_resistor_1 (.node(n74244_2_pin18[0]));
  Pull_Resistor pull_resistor_2 (.node(n74244_2_pin18[1]));
  Pull_Resistor pull_resistor_3 (.node(n74244_2_pin18[2]));
  Pull_Resistor pull_resistor_4 (.node(n74244_2_pin18[3]));
  RAM #(.dataWidth(4), .databus("bidir")) RAM_1 (
    .addr(n74273_2_pin2), .we(n7400_1_pin13), .oe(n7400_1_pin11), .clk(n7400_1_pin4), .data(n74244_2_pin18));
  _74273 u_74273_2 (
    .pin1(n74163_1_pin1), .pin2(n74273_2_pin2[0]), .pin3(n74163_1_pin3), .pin4(n74163_1_pin4),
    .pin5(n74273_2_pin2[1]), .pin6(n74273_2_pin2[2]), .pin7(n74163_1_pin5), .pin8(n74163_1_pin6),
    .pin9(n74273_2_pin2[3]), .pin19(n74273_2_pin2[7]), .pin18(n74163_2_pin6), .pin17(n74163_2_pin5),
    .pin16(n74273_2_pin2[6]), .pin15(n74273_2_pin2[5]), .pin14(n74163_2_pin4), .pin13(n74163_2_pin3),
    .pin12(n74273_2_pin2[4]), .pin11(n7408_2_pin11));
  // also tied to VCC on the sheet: {n74163_1_pin7, n74163_1_pin10, n7474_1_pin4, n7474_1_pin10, n7474_2_pin4, n7474_2_pin10}

  // Notes on the sheet:
  //   contents of ROM_1 (hex, n*v repeats v):
  //   2 2 ff 2 3 2 51 2 13 51 2 23 0 2 33
endmodule

module shift_reg (
  input  D0,
  input  D1,
  input  D2,
  input  D3,
  input  SHIFT,
  input  LOAD,
  output Q0,
  output Q1,
  output Q2,
  output Q3
);

  wire and_1_out, and_2_out, and_3_out, and_4_out, and_5_out, and_6_out, and_7_out, and_8_out, d_ff_1_qn,
       d_ff_2_qn, d_ff_3_qn, not_1_out, not_2_out, not_3_out, not_4_out, not_5_out, not_6_out, not_7_out;

  D_Flip_Flop d_ff_1 (.D(1'b0), .clk(SHIFT), .Q(Q0), .Qn(d_ff_1_qn), .preset(and_1_out), .reset(and_2_out));
  not not_1 (not_1_out, D0);
  and and_1 (and_1_out, D0, LOAD);
  and and_2 (and_2_out, not_1_out, LOAD);
  not not_2 (not_2_out, d_ff_1_qn);
  and and_3 (and_3_out, D1, LOAD);
  D_Flip_Flop d_ff_2 (.D(not_2_out), .clk(SHIFT), .Q(Q1), .Qn(d_ff_2_qn), .preset(and_3_out), .reset(and_4_out));
  and and_4 (and_4_out, not_3_out, LOAD);
  not not_3 (not_3_out, D1);
  not not_4 (not_4_out, d_ff_2_qn);
  and and_5 (and_5_out, D2, LOAD);
  D_Flip_Flop d_ff_3 (.D(not_4_out), .clk(SHIFT), .Q(Q2), .Qn(d_ff_3_qn), .preset(and_5_out), .reset(and_6_out));
  and and_6 (and_6_out, not_5_out, LOAD);
  not not_5 (not_5_out, D2);
  not not_6 (not_6_out, d_ff_3_qn);
  and and_7 (and_7_out, D3, LOAD);
  D_Flip_Flop d_ff_4 (.D(not_6_out), .clk(SHIFT), .Q(Q3), .preset(and_7_out), .reset(and_8_out));  // open: Qn
  and and_8 (and_8_out, not_7_out, LOAD);
  not not_7 (not_7_out, D3);
endmodule

module adder_8bit (
  input  A0,
  input  A1,
  input  A2,
  input  A3,
  input  A4,
  input  A5,
  input  A6,
  input  A7,
  input  B0,
  input  B1,
  input  B2,
  input  B3,
  input  B4,
  input  B5,
  input  B6,
  input  B7,
  output R0,
  output R1,
  output R2,
  output R3,
  output R4,
  output R5,
  output R6,
  output R7
);

  wire and_1_out, and_2_out, and_3_out, and_4_out, and_5_out, and_6_out, and_7_out, and_8_out, and_9_out,
       and_10_out, and_11_out, and_12_out, and_13_out, and_14_out, or_1_out, or_2_out, or_3_out, or_4_out,
       or_5_out, or_6_out, or_7_out, xor_1_out, xor_2_out, xor_3_out, xor_4_out, xor_5_out, xor_6_out,
       xor_7_out, xor_8_out;

  xor xor_1 (xor_1_out, A0, B0);
  xor xor_2 (xor_2_out, A1, B1);
  xor xor_3 (xor_3_out, A2, B2);
  xor xor_4 (xor_4_out, A3, B3);
  xor xor_5 (xor_5_out, A4, B4);
  xor xor_6 (xor_6_out, A5, B5);
  xor xor_7 (xor_7_out, A6, B6);
  xor xor_8 (xor_8_out, A7, B7);
  xor xor_9 (R0, xor_1_out, 1'b0);
  and and_1 (and_1_out, xor_1_out, 1'b0);
  and and_2 (and_2_out, A0, B0);
  xor xor_10 (R1, xor_2_out, or_1_out);
  and and_3 (and_3_out, xor_2_out, or_1_out);
  and and_4 (and_4_out, A1, B1);
  xor xor_11 (R2, xor_3_out, or_2_out);
  and and_5 (and_5_out, xor_3_out, or_2_out);
  and and_6 (and_6_out, A2, B2);
  xor xor_12 (R3, xor_4_out, or_3_out);
  and and_7 (and_7_out, xor_4_out, or_3_out);
  and and_8 (and_8_out, A3, B3);
  xor xor_13 (R4, xor_5_out, or_4_out);
  and and_9 (and_9_out, xor_5_out, or_4_out);
  and and_10 (and_10_out, A4, B4);
  xor xor_14 (R5, xor_6_out, or_5_out);
  and and_11 (and_11_out, xor_6_out, or_5_out);
  and and_12 (and_12_out, A5, B5);
  xor xor_15 (R6, xor_7_out, or_6_out);
  and and_13 (and_13_out, xor_7_out, or_6_out);
  and and_14 (and_14_out, A6, B6);
  xor xor_16 (R7, xor_8_out, or_7_out);
  or or_1 (or_1_out, and_1_out, and_2_out);
  or or_2 (or_2_out, and_3_out, and_4_out);
  or or_3 (or_3_out, and_5_out, and_6_out);
  or or_4 (or_4_out, and_7_out, and_8_out);
  or or_5 (or_5_out, and_9_out, and_10_out);
  or or_6 (or_6_out, and_11_out, and_12_out);
  or or_7 (or_7_out, and_13_out, and_14_out);
endmodule

module multiply (
  input  DIN0,
  input  DIN1,
  input  DIN2,
  input  DIN3,
  input  RSEL,
  input  LOAD,
  input  MUL_CLK,
  output R0,
  output R1,
  output R2,
  output R3
);

  wire adder_8bit_1_r0, adder_8bit_1_r1, adder_8bit_1_r2, adder_8bit_1_r3, adder_8bit_1_r4, adder_8bit_1_r5,
       adder_8bit_1_r6, adder_8bit_1_r7, and_1_out, and_2_out, and_3_out, and_4_out, and_5_out, and_6_out,
       and_7_out, and_8_out, and_9_out, and_10_out, and_11_out, and_12_out, and_13_out, and_14_out,
       and_15_out, and_16_out, and_17_out, and_18_out, and_19_out, and_20_out, d_ff_1_q, d_ff_2_q, d_ff_3_q,
       d_ff_4_q, d_ff_5_q, d_ff_6_q, d_ff_7_q, d_ff_8_q, not_1_out, not_2_out, not_3_out, not_4_out,
       not_5_out, shift_reg_1_q3, shift_reg_8_1_q0, shift_reg_8_1_q1, shift_reg_8_1_q2, shift_reg_8_1_q3,
       shift_reg_8_1_q4, shift_reg_8_1_q5, shift_reg_8_1_q6, shift_reg_8_1_q7, t_ff_1_q, t_ff_2_q, t_ff_3_q;

  not not_1 (not_1_out, and_3_out);
  and and_1 (and_1_out, not_1_out, MUL_CLK);
  and and_2 (and_2_out, and_1_out, t_ff_3_q);
  T_Flip_Flop t_ff_1 (.T(1'b1), .clk(not_2_out), .Q(t_ff_1_q), .preset(and_3_out));  // open: Qn, reset
  not not_2 (not_2_out, and_2_out);
  T_Flip_Flop t_ff_2 (.T(1'b1), .clk(t_ff_1_q), .Q(t_ff_2_q), .preset(and_3_out));  // open: Qn, reset
  and and_3 (and_3_out, LOAD, RSEL);
  not not_3 (not_3_out, and_2_out);
  T_Flip_Flop t_ff_3 (.T(1'b1), .clk(t_ff_2_q), .Q(t_ff_3_q), .preset(and_3_out));  // open: Qn, reset
  not not_4 (not_4_out, RSEL);
  and and_4 (and_4_out, LOAD, not_4_out);
  shift_reg_8 shift_reg_8_1 (
    .D0(DIN0), .D1(DIN1), .D2(DIN2), .D3(DIN3), .SHIFT(not_3_out), .LOAD(and_3_out), .Q0(shift_reg_8_1_q0),
    .Q1(shift_reg_8_1_q1), .Q2(shift_reg_8_1_q2), .Q3(shift_reg_8_1_q3), .Q4(shift_reg_8_1_q4),
    .Q5(shift_reg_8_1_q5), .Q6(shift_reg_8_1_q6), .Q7(shift_reg_8_1_q7));
  shift_reg shift_reg_1 (
    .D0(DIN3), .D1(DIN2), .D2(DIN1), .D3(DIN0), .SHIFT(not_3_out), .LOAD(and_4_out), .Q3(shift_reg_1_q3));  // open: Q0, Q1, Q2
  and and_5 (and_5_out, shift_reg_8_1_q0, shift_reg_1_q3);
  and and_6 (and_6_out, shift_reg_8_1_q1, shift_reg_1_q3);
  and and_7 (and_7_out, shift_reg_8_1_q2, shift_reg_1_q3);
  and and_8 (and_8_out, shift_reg_8_1_q3, shift_reg_1_q3);
  and and_9 (and_9_out, shift_reg_8_1_q4, shift_reg_1_q3);
  and and_10 (and_10_out, shift_reg_8_1_q5, shift_reg_1_q3);
  and and_11 (and_11_out, shift_reg_8_1_q6, shift_reg_1_q3);
  and and_12 (and_12_out, shift_reg_8_1_q7, shift_reg_1_q3);
  adder_8bit adder_8bit_1 (
    .A0(and_5_out), .A1(and_6_out), .A2(and_7_out), .A3(and_8_out), .A4(and_9_out), .A5(and_10_out),
    .A6(and_11_out), .A7(and_12_out), .B0(d_ff_1_q), .B1(d_ff_2_q), .B2(d_ff_3_q), .B3(d_ff_4_q),
    .B4(d_ff_5_q), .B5(d_ff_6_q), .B6(d_ff_7_q), .B7(d_ff_8_q), .R0(adder_8bit_1_r0), .R1(adder_8bit_1_r1),
    .R2(adder_8bit_1_r2), .R3(adder_8bit_1_r3), .R4(adder_8bit_1_r4), .R5(adder_8bit_1_r5),
    .R6(adder_8bit_1_r6), .R7(adder_8bit_1_r7));
  D_Flip_Flop d_ff_1 (.D(adder_8bit_1_r0), .clk(and_2_out), .Q(d_ff_1_q), .reset(LOAD));  // open: Qn, preset
  D_Flip_Flop d_ff_2 (.D(adder_8bit_1_r1), .clk(and_2_out), .Q(d_ff_2_q), .reset(LOAD));  // open: Qn, preset
  D_Flip_Flop d_ff_3 (.D(adder_8bit_1_r2), .clk(and_2_out), .Q(d_ff_3_q), .reset(LOAD));  // open: Qn, preset
  D_Flip_Flop d_ff_4 (.D(adder_8bit_1_r3), .clk(and_2_out), .Q(d_ff_4_q), .reset(LOAD));  // open: Qn, preset
  D_Flip_Flop d_ff_5 (.D(adder_8bit_1_r4), .clk(and_2_out), .Q(d_ff_5_q), .reset(LOAD));  // open: Qn, preset
  D_Flip_Flop d_ff_6 (.D(adder_8bit_1_r5), .clk(and_2_out), .Q(d_ff_6_q), .reset(LOAD));  // open: Qn, preset
  D_Flip_Flop d_ff_7 (.D(adder_8bit_1_r6), .clk(and_2_out), .Q(d_ff_7_q), .reset(LOAD));  // open: Qn, preset
  D_Flip_Flop d_ff_8 (.D(adder_8bit_1_r7), .clk(and_2_out), .Q(d_ff_8_q), .reset(LOAD));  // open: Qn, preset
  not not_5 (not_5_out, RSEL);
  and and_13 (and_13_out, d_ff_1_q, RSEL);
  and and_14 (and_14_out, d_ff_2_q, RSEL);
  and and_15 (and_15_out, d_ff_3_q, RSEL);
  and and_16 (and_16_out, d_ff_4_q, RSEL);
  and and_17 (and_17_out, d_ff_5_q, not_5_out);
  and and_18 (and_18_out, d_ff_6_q, not_5_out);
  and and_19 (and_19_out, d_ff_7_q, not_5_out);
  and and_20 (and_20_out, d_ff_8_q, not_5_out);
  or or_1 (R0, and_13_out, and_17_out);
  or or_2 (R1, and_14_out, and_18_out);
  or or_3 (R2, and_15_out, and_19_out);
  or or_4 (R3, and_16_out, and_20_out);
endmodule

module shift_reg_8 (
  input  D0,
  input  D1,
  input  D2,
  input  D3,
  input  SHIFT,
  input  LOAD,
  output Q0,
  output Q1,
  output Q2,
  output Q3,
  output Q4,
  output Q5,
  output Q6,
  output Q7
);

  wire and_1_out, and_2_out, and_3_out, and_4_out, and_5_out, and_6_out, and_7_out, and_8_out, d_ff_1_qn,
       d_ff_2_qn, d_ff_3_qn, d_ff_4_qn, d_ff_5_qn, d_ff_6_qn, d_ff_7_qn, not_1_out, not_2_out, not_3_out,
       not_4_out, not_5_out, not_6_out, not_7_out, not_8_out, not_9_out, not_10_out, not_11_out;

  D_Flip_Flop d_ff_1 (.D(1'b0), .clk(SHIFT), .Q(Q0), .Qn(d_ff_1_qn), .preset(and_1_out), .reset(and_2_out));
  not not_1 (not_1_out, D0);
  and and_1 (and_1_out, D0, LOAD);
  and and_2 (and_2_out, not_1_out, LOAD);
  not not_2 (not_2_out, d_ff_1_qn);
  and and_3 (and_3_out, D1, LOAD);
  D_Flip_Flop d_ff_2 (.D(not_2_out), .clk(SHIFT), .Q(Q1), .Qn(d_ff_2_qn), .preset(and_3_out), .reset(and_4_out));
  and and_4 (and_4_out, not_3_out, LOAD);
  not not_3 (not_3_out, D1);
  not not_4 (not_4_out, d_ff_2_qn);
  and and_5 (and_5_out, D2, LOAD);
  D_Flip_Flop d_ff_3 (.D(not_4_out), .clk(SHIFT), .Q(Q2), .Qn(d_ff_3_qn), .preset(and_5_out), .reset(and_6_out));
  and and_6 (and_6_out, not_5_out, LOAD);
  not not_5 (not_5_out, D2);
  not not_6 (not_6_out, d_ff_3_qn);
  and and_7 (and_7_out, D3, LOAD);
  D_Flip_Flop d_ff_4 (.D(not_6_out), .clk(SHIFT), .Q(Q3), .Qn(d_ff_4_qn), .preset(and_7_out), .reset(and_8_out));
  and and_8 (and_8_out, not_7_out, LOAD);
  not not_7 (not_7_out, D3);
  not not_8 (not_8_out, d_ff_4_qn);
  D_Flip_Flop d_ff_5 (.D(not_8_out), .clk(SHIFT), .Q(Q4), .Qn(d_ff_5_qn), .reset(LOAD));  // open: preset
  D_Flip_Flop d_ff_6 (.D(not_9_out), .clk(SHIFT), .Q(Q5), .Qn(d_ff_6_qn), .reset(LOAD));  // open: preset
  not not_9 (not_9_out, d_ff_5_qn);
  not not_10 (not_10_out, d_ff_6_qn);
  D_Flip_Flop d_ff_7 (.D(not_10_out), .clk(SHIFT), .Q(Q6), .Qn(d_ff_7_qn), .reset(LOAD));  // open: preset
  D_Flip_Flop d_ff_8 (.D(not_11_out), .clk(SHIFT), .Q(Q7), .reset(LOAD));  // open: Qn, preset
  not not_11 (not_11_out, d_ff_7_qn);
endmodule

module toggle (
  input  RST,
  input  CLK,
  output O_S,
  output CLK1,
  output CLK2
);

  wire and_1_out, and_2_out, and_3_out, and_4_out, and_5_out, and_6_out, and_7_out, and_8_out, and_11_out,
       not_1_out, not_2_out, not_3_out, not_4_out, not_5_out, not_6_out, not_7_out, or_1_out, or_2_out,
       or_3_out, or_4_out, or_5_out, t_ff_1_q;

  T_Flip_Flop t_ff_1 (.T(1'b1), .clk(CLK), .Q(t_ff_1_q));  // open: Qn, reset, preset
  not not_1 (not_1_out, and_8_out);
  not not_2 (not_2_out, t_ff_1_q);
  not not_3 (not_3_out, and_8_out);
  not not_4 (not_4_out, t_ff_1_q);
  and and_1 (and_1_out, not_1_out, t_ff_1_q);
  and and_2 (and_2_out, and_7_out, not_2_out);
  and and_3 (and_3_out, and_7_out, not_3_out);
  and and_4 (and_4_out, and_8_out, t_ff_1_q);
  and and_5 (and_5_out, and_7_out, not_4_out);
  and and_6 (and_6_out, and_8_out, and_7_out);
  or or_1 (or_1_out, and_1_out, and_2_out);
  or or_2 (or_2_out, and_4_out, and_5_out);
  not not_5 (not_5_out, RST);
  or or_3 (or_3_out, or_1_out, and_3_out);
  or or_4 (or_4_out, or_2_out, and_6_out);
  and and_7 (and_7_out, not_5_out, or_3_out);
  and and_8 (and_8_out, not_5_out, or_4_out);
  not not_6 (not_6_out, and_8_out);
  not not_7 (not_7_out, and_7_out);
  and and_9 (CLK1, and_7_out, not_6_out);
  and and_10 (CLK2, and_8_out, not_7_out);
  and and_11 (and_11_out, RST, CLK);
  T_Flip_Flop t_ff_2 (.T(1'b1), .clk(or_5_out), .Q(O_S), .preset(and_11_out));  // open: Qn, reset
  or or_5 (or_5_out, CLK2, CLK1);
endmodule
